// Logisim project ex2.circ as structural Verilog: 1 circuit, main circuit compute_BrUn
module compute_BrUn (
  input  [31:0] INSTRUCTION,
  output BrUn
);

  wire comparator_1_lt, not_1_out;

  Comparator #(.mode("unsigned"), .width(3)) comparator_1 (
    .a(INSTRUCTION[14:12]), .b(3'b010), .lt(comparator_1_lt));  // open: gt, eq
  not not_1 (not_1_out, comparator_1_lt);
  and and_1 (BrUn, INSTRUCTION[13], not_1_out);
endmodule
